// Logisim project Somador Hexa.circ as structural Verilog: 4 circuits, main circuit main
module main (
  input  in_1,
  input  in_2,
  input  in_3,
  input  in_4,
  input  in_5,
  input  in_6,
  input  in_7,
  input  in_8,
  input  in_9,
  input  in_10,
  input  in_11
);

  wire dechex_1_a_2, dechex_1_b_2, dechex_1_c_2, dechex_1_d_2, dechex_1_e, dechex_1_f, dechex_1_g,
       dechex_2_a_2, dechex_2_b_2, dechex_2_c_2, dechex_2_d_2, dechex_2_e, dechex_2_f, dechex_2_g,
       dechex_3_a_2, dechex_3_b_2, dechex_3_c_2, dechex_3_d_2, dechex_3_e, dechex_3_f, dechex_3_g,
       dechex_4_a_2, dechex_4_b_2, dechex_4_c_2, dechex_4_d_2, dechex_4_e, dechex_4_f, dechex_4_g,
       dechex_5_a_2, dechex_5_b_2, dechex_5_c_2, dechex_5_d_2, dechex_5_e, dechex_5_f, dechex_5_g,
       dechex_6_a_2, dechex_6_b_2, dechex_6_c_2, dechex_6_d_2, dechex_6_e, dechex_6_f, dechex_6_g, S1, S2,
       S3, S4, S5, separador_1_a2, separador_1_a_2, separador_1_b2, separador_1_b_2, separador_1_c_2,
       separador_1_d_2, somador_2_carry_2, somador_3_carry_2, somador_4_carry_2;

  DecHex dechex_1 (
    .A(in_1), .B(in_3), .C(in_5), .D(in_7), .a_2(dechex_1_a_2), .b_2(dechex_1_b_2), .c_2(dechex_1_c_2),
    .d_2(dechex_1_d_2), .e(dechex_1_e), .f(dechex_1_f), .g(dechex_1_g));
  Somador somador_1 (.A(in_1), .B(in_2), .Carry(somador_2_carry_2), .S(S4), .Carry_2(S5));
  _7_Segment_Display u_7_segment_display_1 (
    .g(dechex_1_g), .f(dechex_1_f), .a(dechex_1_a_2), .b(dechex_1_b_2), .e(dechex_1_e), .d(dechex_1_d_2),
    .c(dechex_1_c_2));  // open: dp
  Somador somador_2 (.A(in_3), .B(in_4), .Carry(somador_3_carry_2), .S(S3), .Carry_2(somador_2_carry_2));
  Somador somador_3 (.A(in_5), .B(in_6), .Carry(somador_4_carry_2), .S(S2), .Carry_2(somador_3_carry_2));
  DecHex dechex_2 (
    .A(in_2), .B(in_4), .C(in_6), .D(in_8), .a_2(dechex_2_a_2), .b_2(dechex_2_b_2), .c_2(dechex_2_c_2),
    .d_2(dechex_2_d_2), .e(dechex_2_e), .f(dechex_2_f), .g(dechex_2_g));
  Somador somador_4 (.A(in_7), .B(in_8), .Carry(in_10), .S(S1), .Carry_2(somador_4_carry_2));
  _7_Segment_Display u_7_segment_display_2 (
    .g(dechex_2_g), .f(dechex_2_f), .a(dechex_2_a_2), .b(dechex_2_b_2), .e(dechex_2_e), .d(dechex_2_d_2),
    .c(dechex_2_c_2));  // open: dp
  separador separador_1 (
    .A(S5), .B(S4), .C(S3), .D(S2), .E(S1), .a_2(separador_1_a_2), .b_2(separador_1_b_2),
    .c_2(separador_1_c_2), .d_2(separador_1_d_2), .a2(separador_1_a2), .b2(separador_1_b2));
  DecHex dechex_3 (
    .A(in_9), .B(in_9), .C(in_9), .D(S5), .a_2(dechex_3_a_2), .b_2(dechex_3_b_2), .c_2(dechex_3_c_2),
    .d_2(dechex_3_d_2), .e(dechex_3_e), .f(dechex_3_f), .g(dechex_3_g));
  DecHex dechex_4 (
    .A(in_11), .B(in_11), .C(separador_1_a2), .D(separador_1_b2), .a_2(dechex_4_a_2), .b_2(dechex_4_b_2),
    .c_2(dechex_4_c_2), .d_2(dechex_4_d_2), .e(dechex_4_e), .f(dechex_4_f), .g(dechex_4_g));
  _7_Segment_Display u_7_segment_display_3 (
    .g(dechex_3_g), .f(dechex_3_f), .a(dechex_3_a_2), .b(dechex_3_b_2), .e(dechex_3_e), .d(dechex_3_d_2),
    .c(dechex_3_c_2));  // open: dp
  _7_Segment_Display u_7_segment_display_4 (
    .g(dechex_4_g), .f(dechex_4_f), .a(dechex_4_a_2), .b(dechex_4_b_2), .e(dechex_4_e), .d(dechex_4_d_2),
    .c(dechex_4_c_2));  // open: dp
  DecHex dechex_5 (
    .A(separador_1_a_2), .B(separador_1_b_2), .C(separador_1_c_2), .D(separador_1_d_2), .a_2(dechex_5_a_2),
    .b_2(dechex_5_b_2), .c_2(dechex_5_c_2), .d_2(dechex_5_d_2), .e(dechex_5_e), .f(dechex_5_f), .g(dechex_5_g));
  DecHex dechex_6 (
    .A(S4), .B(S3), .C(S2), .D(S1), .a_2(dechex_6_a_2), .b_2(dechex_6_b_2), .c_2(dechex_6_c_2),
    .d_2(dechex_6_d_2), .e(dechex_6_e), .f(dechex_6_f), .g(dechex_6_g));
  _7_Segment_Display u_7_segment_display_5 (
    .g(dechex_5_g), .f(dechex_5_f), .a(dechex_5_a_2), .b(dechex_5_b_2), .e(dechex_5_e), .d(dechex_5_d_2),
    .c(dechex_5_c_2));  // open: dp
  _7_Segment_Display u_7_segment_display_6 (
    .g(dechex_6_g), .f(dechex_6_f), .a(dechex_6_a_2), .b(dechex_6_b_2), .e(dechex_6_e), .d(dechex_6_d_2),
    .c(dechex_6_c_2));  // open: dp

  // Notes on the sheet:
  //   Numero Hexadecimal A
  //   Numero Hexadecimal B
  //   Resposta Hexadecimal
  //   Resposta Decimal
endmodule

module DecHex (
  input  A,
  input  B,
  input  C,
  input  D,
  output a_2,
  output b_2,
  output c_2,
  output d_2,
  output e,
  output f,
  output g
);

  wire and_1_out, and_2_out, and_3_out, and_4_out, and_5_out, and_6_out, and_7_out, and_8_out, and_9_out,
       and_10_out, and_11_out, and_12_out, and_13_out, and_14_out, and_15_out, and_16_out, and_17_out,
       and_18_out, and_19_out, and_20_out, and_21_out, and_22_out, and_23_out, and_24_out, and_25_out,
       and_26_out, and_27_out, and_28_out, and_29_out, and_30_out, and_31_out, and_32_out, and_33_out,
       and_34_out, and_35_out, not_1_out, not_2_out, not_3_out, not_4_out, not_5_out, not_6_out, not_7_out,
       not_8_out, not_9_out, not_10_out, not_11_out, not_12_out, not_13_out, not_14_out, not_15_out,
       not_16_out, not_17_out, not_18_out, not_19_out, not_20_out, not_21_out, not_22_out, not_23_out,
       not_24_out, not_25_out, not_26_out, not_27_out, not_28_out, not_29_out, not_30_out, not_31_out,
       not_32_out, not_33_out, not_34_out, not_35_out, not_36_out, not_37_out, not_38_out, not_39_out,
       not_40_out, not_41_out, not_42_out, not_43_out;

  not not_1 (not_1_out, B);
  and and_1 (and_1_out, not_1_out, not_2_out);
  not not_2 (not_2_out, D);
  not not_3 (not_3_out, A);
  and and_2 (and_2_out, not_3_out, C);
  not not_4 (not_4_out, A);
  and and_3 (and_3_out, not_4_out, B, D);
  and and_4 (and_4_out, B, C);
  not not_5 (not_5_out, B);
  and and_5 (and_5_out, A, not_5_out, not_6_out);
  not not_6 (not_6_out, C);
  and and_6 (and_6_out, A, not_7_out);
  not not_7 (not_7_out, D);
  not not_8 (not_8_out, A);
  and and_7 (and_7_out, not_8_out, not_9_out);
  not not_9 (not_9_out, B);
  not not_10 (not_10_out, A);
  and and_8 (and_8_out, not_10_out, not_11_out, not_12_out);
  not not_11 (not_11_out, C);
  not not_12 (not_12_out, D);
  not not_13 (not_13_out, B);
  and and_9 (and_9_out, not_13_out, not_14_out);
  not not_14 (not_14_out, D);
  not not_15 (not_15_out, A);
  and and_10 (and_10_out, not_15_out, C, D);
  not not_16 (not_16_out, C);
  and and_11 (and_11_out, A, not_16_out, D);
  not not_17 (not_17_out, A);
  and and_12 (and_12_out, not_17_out, not_18_out);
  not not_18 (not_18_out, C);
  not not_19 (not_19_out, A);
  and and_13 (and_13_out, not_19_out, D);
  not not_20 (not_20_out, C);
  and and_14 (and_14_out, not_20_out, D);
  not not_21 (not_21_out, A);
  and and_15 (and_15_out, not_21_out, B);
  and and_16 (and_16_out, A, not_22_out);
  not not_22 (not_22_out, B);
  not not_23 (not_23_out, A);
  and and_17 (and_17_out, not_23_out, not_24_out, not_25_out);
  not not_24 (not_24_out, B);
  not not_25 (not_25_out, D);
  not not_26 (not_26_out, B);
  and and_18 (and_18_out, not_26_out, C, D);
  and and_19 (and_19_out, B, not_27_out, D);
  not not_27 (not_27_out, C);
  and and_20 (and_20_out, B, C, not_28_out);
  not not_28 (not_28_out, D);
  and and_21 (and_21_out, A, not_29_out);
  not not_29 (not_29_out, C);
  not not_30 (not_30_out, B);
  and and_22 (and_22_out, not_30_out, not_31_out);
  not not_31 (not_31_out, D);
  and and_23 (and_23_out, C, not_32_out);
  not not_32 (not_32_out, D);
  and and_24 (and_24_out, A, C);
  and and_25 (and_25_out, A, B);
  not not_33 (not_33_out, C);
  and and_26 (and_26_out, not_33_out, not_34_out);
  not not_34 (not_34_out, D);
  not not_35 (not_35_out, A);
  and and_27 (and_27_out, not_35_out, B, not_36_out);
  not not_36 (not_36_out, C);
  and and_28 (and_28_out, B, not_37_out);
  not not_37 (not_37_out, D);
  and and_29 (and_29_out, A, not_38_out);
  not not_38 (not_38_out, B);
  and and_30 (and_30_out, A, C);
  not not_39 (not_39_out, B);
  and and_31 (and_31_out, not_39_out, C);
  and and_32 (and_32_out, C, not_40_out);
  not not_40 (not_40_out, D);
  not not_41 (not_41_out, A);
  and and_33 (and_33_out, not_41_out, B, not_42_out);
  not not_42 (not_42_out, C);
  and and_34 (and_34_out, A, not_43_out);
  not not_43 (not_43_out, B);
  and and_35 (and_35_out, A, D);
  or or_1 (b_2, and_7_out, and_8_out, and_9_out, and_10_out, and_11_out);
  or or_2 (c_2, and_12_out, and_13_out, and_14_out, and_15_out, and_16_out);
  or or_3 (d_2, and_17_out, and_18_out, and_19_out, and_20_out, and_21_out);
  or or_4 (e, and_22_out, and_23_out, and_24_out, and_25_out);
  or or_5 (f, and_26_out, and_27_out, and_28_out, and_29_out, and_30_out);
  or or_6 (g, and_31_out, and_32_out, and_33_out, and_34_out, and_35_out);
  or or_7 (a_2, and_1_out, and_2_out, and_3_out, and_4_out, and_5_out, and_6_out);
endmodule

module Somador (
  input  A,
  input  B,
  input  Carry,
  output S,
  output Carry_2
);

  wire and_1_out, and_2_out, and_3_out, and_4_out, and_5_out, and_6_out, and_7_out, not_1_out, not_2_out,
       not_3_out, not_4_out, not_5_out, not_6_out;

  not not_1 (not_1_out, A);
  not not_2 (not_2_out, B);
  not not_3 (not_3_out, A);
  not not_4 (not_4_out, Carry);
  not not_5 (not_5_out, B);
  not not_6 (not_6_out, Carry);
  and and_1 (and_1_out, B, Carry);
  and and_2 (and_2_out, A, Carry);
  and and_3 (and_3_out, A, B);
  and and_4 (and_4_out, not_1_out, not_2_out, Carry);
  and and_5 (and_5_out, not_3_out, B, not_4_out);
  and and_6 (and_6_out, A, not_5_out, not_6_out);
  and and_7 (and_7_out, A, B, Carry);
  or or_1 (Carry_2, and_1_out, and_2_out, and_3_out);
  or or_2 (S, and_4_out, and_5_out, and_6_out, and_7_out);
endmodule

module separador (
  input  A,
  input  B,
  input  C,
  input  D,
  input  E,
  output a_2,
  output b_2,
  output c_2,
  output d_2,
  output a2,
  output b2
);

  wire and_1_out, and_2_out, and_3_out, and_4_out, and_5_out, and_6_out, and_7_out, and_8_out, and_9_out,
       and_10_out, and_11_out, and_12_out, and_13_out, and_14_out, and_15_out, and_16_out, and_17_out,
       and_18_out, not_1_out, not_2_out, not_3_out, not_4_out, not_5_out, not_6_out, not_7_out, not_8_out,
       not_9_out, not_10_out, not_11_out, not_12_out, not_13_out, not_14_out, not_15_out, not_16_out,
       not_17_out, not_18_out, not_19_out, not_20_out, not_21_out, not_22_out, not_23_out, not_24_out,
       not_25_out;

  not not_1 (not_1_out, A);
  not not_2 (not_2_out, C);
  not not_3 (not_3_out, D);
  not not_4 (not_4_out, B);
  not not_5 (not_5_out, C);
  not not_6 (not_6_out, D);
  not not_7 (not_7_out, A);
  not not_8 (not_8_out, B);
  not not_9 (not_9_out, A);
  not not_10 (not_10_out, C);
  not not_11 (not_11_out, D);
  not not_12 (not_12_out, C);
  not not_13 (not_13_out, A);
  not not_14 (not_14_out, B);
  not not_15 (not_15_out, B);
  not not_16 (not_16_out, A);
  not not_17 (not_17_out, D);
  not not_18 (not_18_out, B);
  not not_19 (not_19_out, C);
  not not_20 (not_20_out, D);
  not not_21 (not_21_out, C);
  and and_1 (and_1_out, A, C);
  and and_2 (and_2_out, A, B);
  not not_22 (not_22_out, A);
  not not_23 (not_23_out, A);
  not not_24 (not_24_out, B);
  not not_25 (not_25_out, C);
  and and_3 (and_3_out, not_1_out, B, not_2_out, not_3_out);
  and and_4 (and_4_out, A, not_4_out, not_5_out, D);
  and and_5 (and_5_out, A, B, C, not_6_out);
  and and_6 (and_6_out, not_7_out, not_8_out, C);
  and and_7 (and_7_out, not_9_out, C, D);
  and and_8 (and_8_out, A, not_10_out, not_11_out);
  and and_9 (and_9_out, A, B, not_12_out);
  and and_10 (and_10_out, not_13_out, not_14_out, D);
  and and_11 (and_11_out, not_15_out, C, D);
  and and_12 (and_12_out, not_16_out, B, C, not_17_out);
  and and_13 (and_13_out, A, not_18_out, not_19_out, not_20_out);
  and and_14 (and_14_out, A, B, not_21_out, D);
  or or_1 (a2, and_1_out, and_2_out);
  and and_15 (and_15_out, not_22_out, B, D);
  and and_16 (and_16_out, not_23_out, B, C);
  and and_17 (and_17_out, B, C, D);
  and and_18 (and_18_out, A, not_24_out, not_25_out);
  or or_2 (a_2, and_3_out, and_4_out, and_5_out);
  or or_3 (b_2, and_6_out, and_7_out, and_8_out, and_9_out);
  or or_4 (c_2, and_10_out, and_11_out, and_12_out, and_13_out, and_14_out);
  or or_5 (b2, and_15_out, and_16_out, and_17_out, and_18_out);

  assign d_2 = E;
endmodule
